// Digital circuit controlUnit.dig as structural Verilog
// generates control signals for datapath
module controlUnit (
  input  clock,
  input  reset,
  input  [15:0] dIn,
  input  alt,
  input  NE,
  input  GE,
  output wr,
  output rd,
  output sign,
  output word,
  output sub,
  output \logic ,
  output [1:0] logSelect,
  output [11:0] topImm,
  output even,
  output const2,
  output selImm,
  output selConst,
  output Azero,
  output we,
  output [3:0] Rw,
  output [3:0] Ra,
  output [3:0] Rb,
  output selRd,
  output slt,
  output immLow
);

  wire and_1_out, and_3_out, and_4_out, E, F, IR2, IR3, or_1_out;
  wire [11:0] multiplexer_1_out;
  wire [15:8] IR_q;

  Multiplexer multiplexer_1 (.in_0(Rb[0]), .in_1(1'b0), .out(multiplexer_1_out[0]));  // open: sel
  and and_1 (and_1_out, ~dIn[0], ~dIn[1], ~dIn[2], ~dIn[3], F);  // And
  Register #(.Bits(16)) IR (.D(dIn), .C(clock), .Q({IR_q, Rb, IR3, IR2, logSelect}));  // open: en
  D_FF #(.Bits(12)) IM (.D(multiplexer_1_out), .C(clock), .Q(topImm));  // open: nQ
  D_FF fetch (.D(or_1_out), .C(clock), .Q(F), .nQ(E));
  or or_1 (or_1_out, E, reset, and_1_out);
  // And and_2 has open pins: In_1=Rb[0], In_2=Rb[1], In_3=Rb[2], In_4=Rb[3], out=open
  and and_3 (and_3_out, E, ~IR2, ~logSelect[1], ~logSelect[0]);  // And
  and and_4 (and_4_out, E, ~IR3, IR2);  // And
  or or_2 (selRd, and_3_out, and_4_out);
  r0 r0_1 (.rin(IR_q[11:8]), .rout(Ra));  // open: pc, z
  and and_5 (wr, E, ~IR3, IR2, logSelect[1]);  // And
  or or_3 (rd, F, ~logSelect[1]);  // Or
  and and_6 (sub, E, ~IR2, logSelect[1]);  // And
  and and_7 (\logic , E, IR3, IR2);
  r0 r0_2 (.rin(IR_q[15:12]), .rout(Rw));  // open: pc, z
  and and_8 (slt, E, ~IR2, logSelect[1], logSelect[0]);  // And
  not not_1 (sign, IR3);
  // Pins of 1 and 12 bits meet at multiplexer_1_out
  // Pins of 1 and 12 bits meet at {IR_q, Rb}
  // Pins of 1 and 12 bits meet at {12{1'b0}}

  assign word = logSelect[0];

  // Other names for the same wires on the sheet: IR0 = logSelect[0]; IR1 = logSelect[1]

  // Notes on the sheet:
  //   clock: controls internal registers
  //   reset: when high forces the PC to 0x0000
  //   dIn: data from memory
  //   alt: immediate value indicates alternative instruction in lowest bit
  //   NE: A ~= B
  //   GE: A >= B
  //   wr: memory write cycle
  //   rd: memory read cycle
  //   sign: not LBU
  //   word: not SB, LB or LBU
  //   sub: change addition to subtraction
  //   logic: select logic operation instead of addition
  //   logSelect: selects between shift right, AND, OR, XOR
  //   topImm: saved from prefix instruction
  //   even: forces bottom bit of immediate to 0
  //   const2: changes constant from 0 to 2
  //   selImm: B is immediate
  //   selConst: B is a constant
  //   Azero: force A to 0
  //   we: updates register Rw
  //   Rw: register to be written
  //   Ra: first register to read
  //   Rb: second register to read
  //   selRd: selects betweenALU result and memory for write back
  //   slt: ignores ALU result and use GE?0x0000:0x0001
  //   immLow: selects either field rS2 or rD for the 4 lower bits of immediate
endmodule
