// Digital circuit drv16.dig as structural Verilog
// 16 bit processor which is compatible at the assembly language level with RISC-V
module drv16 (
  input  clock,
  input  reset,
  input  [15:0] dIn,
  output [14:0] addr,
  output wr,
  output [15:0] dOut,
  output rd
);

  wire bytes_1_p2;

  RegisterFile #(.AddrBits(4), .Bits(16)) registerfile_1 ();  // open: Din, we, Rw, C, Ra, Rb, Da, Db
  alu alu_1 ();  // open: R, A, B, sub, logSelect, logic, NE, GE
  // bytes bytes_1: pin names not known; wires that end beside it: dIn, bytes_1_p2, dOut

  assign rd = 1'b1;
  assign wr = reset;

  // Notes on the sheet:
  //   addr: selects a 16 bit word in memory to be read or changed
  //   wr: indicates a write operation
  //   dOut: word to be sent to memory
  //   reset: when high prepares the processor to execute from address 0
  //   dIn: word coming from memory
  //   rd: indicates that memory will be read in this cycle
endmodule
